// Logisim project ALU.circ as structural Verilog: 1 circuit, main circuit ALU
module ALU (
  input  [31:0] A,
  input  [31:0] B,
  input  [4:0] Shift,
  input  [3:0] Codop,
  input  CarryIn,
  output [31:0] S,
  output [3:0] Flags
);

  wire A_SIGN_BIT, B_SIGN_BIT, bitselector_6_out, bitselector_7_out, bitselector_9_out, bitselector_10_out,
       C_ADC, C_ASR, C_CMN, C_CMP, C_LSL, C_LSR, C_RSB, C_SBC, V_ADC, V_CMN, V_CMP, V_RSB, V_SBC, xnor_1_out,
       xnor_2_out, xnor_3_out, xnor_4_out, xor_2_out, xor_3_out, xor_4_out, xor_5_out;
  wire [4:0] subtractor_5_out, subtractor_6_out, subtractor_7_out;
  wire [31:0] ADC, ASR, BIC, bit_extender_1_out, CMN, CMP, EOR, ET, LSL, LSR, MUL, MVN, not_1_out, ORR, R,
       RSB, SBC, subtractor_1_out, subtractor_2_out, TST;

  BitSelector #(.width(32)) bitselector_1 (.in(A), .out(A_SIGN_BIT), .sel({5{1'b1}}));
  BitSelector #(.width(32)) bitselector_2 (.in(B), .out(B_SIGN_BIT), .sel({5{1'b1}}));
  assign bit_extender_1_out = {{31{CarryIn}}, CarryIn};  // Bit_Extender bit_extender_1
  assign not_1_out = ~A;  // NOT_Gate not_1, 32 bits wide
  assign ET = A & B;  // AND_Gate and_1, 32 bits wide
  assign EOR = A ^ B;  // XOR_Gate xor_1, 32 bits wide
  Shifter #(.width(32)) shifter_1 (.in(B), .\dist (Shift), .out(LSL));
  Shifter #(.shift("lr"), .width(32)) shifter_2 (.in(B), .\dist (Shift), .out(LSR));
  Shifter #(.shift("ar"), .width(32)) shifter_3 (.in(B), .\dist (Shift), .out(ASR));
  Adder #(.width(32)) adder_1 (.a(A), .b(B), .out(ADC), .cin(CarryIn), .cout(C_ADC));
  Subtractor #(.width(32)) subtractor_1 (.a(B), .b(A), .out(subtractor_1_out));  // open: bin, bout
  Subtractor #(.width(32)) subtractor_2 (.a(bit_extender_1_out), .b(32'h1), .out(subtractor_2_out));  // open: bin, bout
  Shifter #(.shift("rr"), .width(32)) shifter_4 (.in(B), .\dist (Shift), .out(R));
  assign TST = A & B;  // AND_Gate and_2, 32 bits wide
  Subtractor #(.width(32)) subtractor_3 (.a({32{1'b0}}), .b(A), .out(RSB), .bout(C_RSB));  // open: bin
  Subtractor #(.width(32)) subtractor_4 (.a(B), .b(A), .out(CMP), .bout(C_CMP));  // open: bin
  Adder #(.width(32)) adder_2 (.a(A), .b(B), .out(CMN), .cout(C_CMN));  // open: cin
  assign ORR = A | B;  // OR_Gate or_1, 32 bits wide
  Multiplier #(.width(32)) multiplier_1 (.a(A), .b(B), .out(MUL));  // open: cin, cout
  assign BIC = B & not_1_out;  // AND_Gate and_3, 32 bits wide
  assign MVN = ~A;  // NOT_Gate not_2, 32 bits wide
  Adder #(.width(32)) adder_3 (.a(subtractor_1_out), .b(subtractor_2_out), .out(SBC), .cout(C_SBC));  // open: cin
  BitSelector #(.width(32)) bitselector_3 (.in(B), .out(C_LSL), .sel(subtractor_5_out));
  Subtractor #(.width(5)) subtractor_5 (.a({5{1'b0}}), .b(Shift), .out(subtractor_5_out));  // open: bin, bout
  BitSelector #(.width(32)) bitselector_4 (.in(B), .out(C_LSR), .sel(subtractor_6_out));
  Subtractor #(.width(5)) subtractor_6 (.a(Shift), .b(5'b00001), .out(subtractor_6_out));  // open: bin, bout
  BitSelector #(.width(32)) bitselector_5 (.in(B), .out(C_ASR), .sel(subtractor_7_out));
  Subtractor #(.width(5)) subtractor_7 (.a(Shift), .b(5'b00001), .out(subtractor_7_out));  // open: bin, bout
  BitSelector #(.width(32)) bitselector_6 (.in(ADC), .out(bitselector_6_out), .sel({5{1'b1}}));
  BitSelector #(.width(32)) bitselector_7 (.in(ADC), .out(bitselector_7_out), .sel({5{1'b1}}));
  BitSelector #(.width(32)) bitselector_8 (.in(R), .out(C_LSR), .sel({5{1'b1}}));
  BitSelector #(.width(32)) bitselector_9 (.in(ADC), .out(bitselector_9_out), .sel({5{1'b1}}));
  BitSelector #(.width(32)) bitselector_10 (.in(ADC), .out(bitselector_10_out), .sel({5{1'b1}}));
  xor xor_2 (xor_2_out, A_SIGN_BIT, B_SIGN_BIT);
  xor xor_3 (xor_3_out, bitselector_6_out, A_SIGN_BIT);
  xnor xnor_1 (xnor_1_out, A_SIGN_BIT, B_SIGN_BIT);
  xnor xnor_2 (xnor_2_out, bitselector_7_out, A_SIGN_BIT);
  Comparator #(.width(32)) comparator_1 (.a(A), .b(32'h80000000), .eq(V_RSB));  // open: gt, lt
  xor xor_4 (xor_4_out, A_SIGN_BIT, B_SIGN_BIT);
  xor xor_5 (xor_5_out, bitselector_9_out, A_SIGN_BIT);
  xnor xnor_3 (xnor_3_out, A_SIGN_BIT, B_SIGN_BIT);
  xnor xnor_4 (xnor_4_out, bitselector_10_out, A_SIGN_BIT);
  and and_4 (V_ADC, xor_2_out, xor_3_out);
  and and_5 (V_CMP, xor_4_out, xor_5_out);
  and and_6 (V_CMN, xnor_3_out, xnor_4_out);
  and and_7 (V_SBC, xnor_1_out, xnor_2_out);
  Multiplexer #(.select(4), .width(32)) multiplexer_1 (
    .in0(ET), .in1(EOR), .in2(LSL), .in3(LSR), .in4(ASR), .in5(ADC), .in6(SBC), .in7(R), .in9(RSB),
    .in12(ORR), .in13(MUL), .in14(BIC), .in15(MVN), .out(S), .sel(Codop));  // open: in8, in10, in11
  Multiplexer #(.select(4)) multiplexer_2 (
    .in0(1'b0), .in1(1'b0), .in2(C_LSL), .in3(C_LSR), .in4(C_ASR), .in5(C_ADC), .in6(C_SBC), .in7(C_LSR),
    .in8(1'b0), .in9(C_RSB), .in10(C_CMP), .in11(C_CMN), .in12(1'b0), .in13(1'b0), .in14(1'b0), .in15(1'b0),
    .out(Flags[2]), .sel(Codop));
  Multiplexer #(.select(4)) multiplexer_3 (
    .in0(1'b0), .in1(1'b0), .in2(1'b0), .in3(1'b0), .in4(1'b0), .in5(V_ADC), .in6(V_SBC), .in7(1'b0),
    .in8(1'b0), .in9(V_RSB), .in10(V_CMP), .in11(V_CMN), .in12(1'b0), .in13(1'b0), .in14(1'b0), .in15(1'b0),
    .out(Flags[3]), .sel(Codop));
  Comparator #(.width(32)) comparator_2 (.a(S), .b({32{1'b0}}), .eq(Flags[1]), .lt(Flags[0]));  // open: gt
  Comparator #(.width(32)) comparator_3 (.b({32{1'b1}}));  // open: a, gt, eq, lt

  // Other names for the same wires on the sheet: CIn = CarryIn; Co[3:0] = Codop; N = Flags[0]; Z = Flags[1];
  //   C = Flags[2]; V = Flags[3]; S_t[4:0] = Shift

  // Notes on the sheet:
  //   Note: for ROR, C = N
  //   Note 2: assume that shift > 0 for LSL and LSR
endmodule
