// Logisim project Ctl_Conditional.circ as structural Verilog: 1 circuit, main circuit Conditional
module Conditional (
  input  Enable,
  input  [15:0] Instruction,
  input  Z,
  input  C,
  input  N,
  input  V,
  output [10:0] Offset,
  output Verified
);

  wire BITS13, CC_LO, GE, GT, HI, LE, LS, LT, NE, not_5_out, not_6_out, not_7_out, PL, undriven, VC,
       xnor_2_out, xor_2_out;
  wire [3:0] CODE_COND;
  wire [7:0] bitselector_3_out;
  wire [10:0] IMM8, IMM11, multiplexer_1_out;

  not not_1 (NE, Z);
  not not_2 (CC_LO, C);
  not not_3 (PL, N);
  not not_4 (VC, V);
  not not_5 (not_5_out, Z);
  not not_6 (not_6_out, C);
  not not_7 (not_7_out, Z);
  BitSelector #(.width(16)) bitselector_1 (.in(Instruction), .out(BITS13), .sel(4'b1101));
  and and_1 (HI, C, not_5_out);
  or or_1 (LS, not_6_out, Z);
  xnor xnor_1 (GE, V, N);
  xor xor_1 (LT, V, N);
  xnor xnor_2 (xnor_2_out, V, N);
  xor xor_2 (xor_2_out, V, N);
  BitSelector #(.group(11), .width(16)) bitselector_2 (.in(Instruction), .out(IMM11), .sel(undriven));
  assign IMM8 = {{3{bitselector_3_out[7]}}, bitselector_3_out};  // Bit_Extender bit_extender_1
  BitSelector #(.group(8), .width(16)) bitselector_3 (.in(Instruction), .out(bitselector_3_out), .sel(1'b0));
  BitSelector #(.group(4), .width(16)) bitselector_4 (.in(Instruction), .out(CODE_COND), .sel(2'b10));
  and and_2 (GT, not_7_out, xnor_2_out);
  and and_3 (LE, Z, xor_2_out);
  Multiplexer #(.enable("false"), .width(11)) multiplexer_1 (
    .in0(IMM8), .in1(IMM11), .out(multiplexer_1_out), .sel(BITS13));
  Multiplexer #(.enable("false"), .select(4)) multiplexer_2 (
    .in0(Z), .in1(NE), .in2(C), .in3(CC_LO), .in4(N), .in5(PL), .in6(V), .in7(VC), .in8(HI), .in9(LS),
    .in10(GE), .in11(LT), .in12(GT), .in13(LE), .in14(1'b1), .in15(1'b1), .out(Verified), .sel(CODE_COND));
  Multiplexer #(.enable("false"), .width(11)) multiplexer_3 (
    .in0({11{1'b0}}), .in1(multiplexer_1_out), .out(Offset), .sel(Enable));

  // Other names for the same wires on the sheet: CS_HS = C; FLAG_C = C; EQ = Z; FLAG_Z = Z; FLAG_N = N; MI = N;
  //   MUX_OUT = Verified; NEW_OFFSET[10:0] = Offset; FLAG_V = V; VS = V
endmodule
