// Logisim project Ctl_Data_Processing.circ as structural Verilog
module Data_Processing (
  input  Enable,
  input  [15:0] Instruction,
  output [2:0] Rd,
  output [2:0] Rn,
  output [2:0] Rm,
  output [3:0] ALU_Opcode,
  output [3:0] Flags_Update_Mask
);

  wire [2:0] OUT_N, Rd_IN, RD_OUT_1, RD_OUT_2, RD_OUT_3, RD_OUT_4, RD_OUT_5, Rm_IN, RM_OUT_1, RM_OUT_2,
       RM_OUT_3, RM_OUT_5, Rn_IN, RN_OUT_4;
  wire [3:0] flag_update_circ_1_flag_update;

  Demultiplexer #(.select(3), .width(6)) demultiplexer_1 (
    .out0({RM_OUT_1, RD_OUT_1}), .out1({RM_OUT_2, RD_OUT_2}), .out2({RM_OUT_3, RD_OUT_3}),
    .out3({RN_OUT_4, RD_OUT_4}), .out4({RM_OUT_5, RD_OUT_5}), .in(Instruction[5:0]), .sel(OUT_N));  // open: out5, out6, out7
  spec_entry spec_entry_1 (.OPCODE_IN(Instruction[9:6]), .OUT_N(OUT_N));
  Multiplexer #(.select(3), .width(3)) multiplexer_1 (
    .in0(RD_OUT_1), .in1(RD_OUT_2), .in2(RD_OUT_3), .in3(RD_OUT_4), .in4(RD_OUT_5), .out(Rd_IN), .sel(OUT_N));  // open: in5, in6, in7
  Multiplexer #(.select(3), .width(3)) multiplexer_2 (
    .in0(RD_OUT_1), .in1(RD_OUT_2), .in2(RM_OUT_3), .in3(RN_OUT_4), .in4(RD_OUT_5), .out(Rn_IN), .sel(OUT_N));  // open: in5, in6, in7
  Multiplexer #(.select(3), .width(3)) multiplexer_3 (
    .in0(RM_OUT_1), .in1(RM_OUT_2), .in2(RM_OUT_3), .in3(RD_OUT_4), .in4(RM_OUT_5), .out(Rm_IN), .sel(OUT_N));  // open: in5, in6, in7
  flag_update_circ flag_update_circ_1 (.opcode(Instruction[9:6]), .FLAG_UPDATE(flag_update_circ_1_flag_update));
  Multiplexer #(.width(3)) multiplexer_4 (.in0(3'b000), .in1(Rd_IN), .out(Rd), .sel(Enable));
  Multiplexer #(.width(3)) multiplexer_5 (.in0(3'b000), .in1(Rn_IN), .out(Rn), .sel(Enable));
  Multiplexer #(.width(3)) multiplexer_6 (.in0(3'b000), .in1(Rm_IN), .out(Rm), .sel(Enable));
  Multiplexer #(.width(4)) multiplexer_7 (.in0(4'b0000), .in1(Instruction[9:6]), .out(ALU_Opcode), .sel(Enable));
  Multiplexer #(.width(4)) multiplexer_8 (
    .in0(4'b0000), .in1(flag_update_circ_1_flag_update), .out(Flags_Update_Mask), .sel(Enable));

  // Other names for the same wires on the sheet: RN_OUT_1[2:0] = RD_OUT_1; RN_OUT_2[2:0] = RD_OUT_2;
  //   RN_OUT_3[2:0] = RM_OUT_3; RM_OUT_4[2:0] = RD_OUT_4; RN_OUT_5[2:0] = RD_OUT_5; Rndm[5:0] = Instruction[5:0];
  //   OPCODE_OUT[3:0] = Instruction[9:6]

  // Notes on the sheet:
  //   Note 2: RSB instruction has Rn as 1st operand.
  //   MUL instruction has Rn as 1st operand and Rdm as 2nd operand
  //   For simplification purposes, Rm is used for 1st operand both here and in the ALU.
  //   Pull output low on Enable = 0
  //   Note: instructions that does not save the result will still have the second operand as the destination register, the ALU will copy the second register to the destination register
endmodule

module spec_entry (
  input  [3:0] OPCODE_IN,
  output [2:0] OUT_N
);

  wire and_3_out, and_4_out, and_5_out, not_1_out, not_2_out, not_3_out;

  not not_1 (not_1_out, OPCODE_IN[2]);
  not not_2 (not_2_out, OPCODE_IN[1]);
  not not_3 (not_3_out, OPCODE_IN[0]);
  and and_1 (OUT_N[2], OPCODE_IN[3], OPCODE_IN[2], OPCODE_IN[1], OPCODE_IN[0]);
  and and_2 (OUT_N[1], OPCODE_IN[3], not_2_out, OPCODE_IN[0]);
  and and_3 (and_3_out, OPCODE_IN[3], not_1_out, not_3_out);
  and and_4 (and_4_out, OPCODE_IN[3], not_1_out, OPCODE_IN[1]);
  or or_1 (OUT_N[0], and_3_out, and_4_out, and_5_out);
  and and_5 (and_5_out, OPCODE_IN[3], OPCODE_IN[2], not_2_out, OPCODE_IN[0]);
endmodule

module flag_update_circ (
  input  [3:0] opcode,
  output [3:0] FLAG_UPDATE
);

  Multiplexer #(.select(4), .width(4)) multiplexer_1 (
    .in0(4'b1110), .in1(4'b1110), .in2(4'b1110), .in3(4'b1110), .in4(4'b1110), .in5(4'b1111), .in6(4'b1111),
    .in7(4'b1110), .in8(4'b1110), .in9(4'b1111), .in10(4'b1111), .in11(4'b1111), .in12(4'b1110),
    .in13(4'b1100), .in14(4'b1110), .in15(4'b1110), .out(FLAG_UPDATE), .sel(opcode));
endmodule
