// Logisim project Ctl_Load_Store.circ as structural Verilog: 1 circuit, main circuit Load_Store
module Load_Store (
  input  Enable,
  input  [15:0] Instruction,
  input  [31:0] Stack_Pointer,
  input  Clk,
  input  Reset,
  output Store,
  output Load,
  output [2:0] Rmd,
  output [31:0] RAM_Addr,
  output PC_Hold
);

  wire and_1_out, not_1_out, not_2_out;
  wire [2:0] bit_extender_2_out;
  wire [31:0] bit_extender_1_out, bit_extender_3_out, RAM_Addr_t;

  assign bit_extender_1_out = {{24{Instruction[7]}}, Instruction[7:0]};  // Bit_Extender bit_extender_1
  Adder #(.width(32)) adder_1 (.a(bit_extender_1_out), .b(Stack_Pointer), .out(RAM_Addr_t));  // open: cin, cout
  not not_1 (not_1_out, Instruction[11]);
  assign bit_extender_2_out = {{2{Enable}}, Enable};  // Bit_Extender bit_extender_2
  assign bit_extender_3_out = {{31{Enable}}, Enable};  // Bit_Extender bit_extender_3
  not not_2 (not_2_out, PC_Hold);
  and and_1 (and_1_out, Instruction[11], not_2_out);
  and and_2 (Store, not_1_out, Enable);
  and and_3 (Load, Enable, Instruction[11]);
  assign Rmd = Instruction[10:8] & bit_extender_2_out;  // AND_Gate and_4, 3 bits wide
  assign RAM_Addr = RAM_Addr_t & bit_extender_3_out;  // AND_Gate and_5, 32 bits wide
  D_Flip_Flop d_ff_1 (.D(and_1_out), .clk(Clk), .Q(PC_Hold), .reset(Reset));  // open: Qn, preset

  // Other names for the same wires on the sheet: imm8[7:0] = Instruction[7:0]; Rt[2:0] = Instruction[10:8];
  //   L_R = Instruction[11]

  // Notes on the sheet:
  //   Instruction: pull=down
  //   Delay load and hold PC for 1 cycle for the RAM to send out requested data 
endmodule
