// Logisim project Ctl_Opcode_Decoder.circ as structural Verilog: 2 circuits, main circuit Opcode_Decoder
module Opcode_Decoder (
  input  [5:0] Opcode,
  output Shift,
  output Data_Processing,
  output Load_Store,
  output SP_Address,
  output Conditional
);

  SC_OPCODERDECODER sc_opcoderdecoder_1 (
    .Opcode(Opcode), .Shift(Shift), .Data_Processing(Data_Processing), .Load_Store(Load_Store),
    .SP_Address(SP_Address), .Conditional(Conditional));

  // Notes on the sheet:
  //   Shift, add, sub, mov
  //   Load/Store
  //   SP Address
  //   Data Processing
  //   Conditional branch
endmodule

module SC_OPCODERDECODER (
  input  [5:0] Opcode,
  output Shift,
  output Data_Processing,
  output Load_Store,
  output SP_Address,
  output Conditional
);

  wire and_1_out, and_2_out, and_3_out, and_4_out, and_5_out, and_6_out, and_7_out, and_8_out, and_9_out,
       and_10_out, and_11_out, not_1_out, not_2_out, not_3_out, not_4_out;

  not not_1 (not_1_out, Opcode[5]);
  not not_2 (not_2_out, Opcode[4]);
  not not_3 (not_3_out, Opcode[3]);
  not not_4 (not_4_out, Opcode[2]);
  and and_1 (and_1_out, not_1_out, not_2_out);
  and and_2 (and_2_out, Opcode[5], Opcode[4], Opcode[3], Opcode[2], Opcode[1], Opcode[0]);
  and and_3 (and_3_out, not_1_out, Opcode[4]);
  and and_4 (and_4_out, Opcode[4], Opcode[3], Opcode[2], Opcode[1], Opcode[0]);
  and and_5 (and_5_out, Opcode[5], not_2_out, not_3_out, Opcode[2]);
  and and_6 (and_6_out, Opcode[5], Opcode[4], Opcode[3], Opcode[2], Opcode[1], Opcode[0]);
  and and_7 (and_7_out, Opcode[5], not_2_out, Opcode[3], Opcode[2]);
  and and_8 (and_8_out, Opcode[5], Opcode[3], Opcode[2], Opcode[1], Opcode[0]);
  and and_9 (and_9_out, Opcode[5], Opcode[4], not_3_out, Opcode[2]);
  and and_10 (and_10_out, Opcode[5], Opcode[4], Opcode[3], not_4_out);
  and and_11 (and_11_out, Opcode[5], Opcode[4], Opcode[2], Opcode[1], Opcode[0]);
  or or_1 (Shift, and_1_out, and_2_out);
  or or_2 (Data_Processing, and_3_out, and_4_out);
  or or_3 (Load_Store, and_5_out, and_6_out);
  or or_4 (SP_Address, and_7_out, and_8_out);
  or or_5 (Conditional, and_9_out, and_10_out, and_11_out);
endmodule
