// Logisim project Ctl_SP_Address.circ as structural Verilog: 1 circuit, main circuit SP_Address
module SP_Address (
  input  [31:0] Stack_Pointer,
  input  [15:0] Instruction,
  input  Enable,
  output [31:0] New_Stack_Pointer,
  output Write_Enable
);

  wire [31:0] ADD, bit_extender_1_out, bit_extender_2_out, MUX_OUTPUT, SUB;

  assign bit_extender_1_out = {{25{1'b0}}, Instruction[6:0]};  // Bit_Extender bit_extender_1
  assign bit_extender_2_out = {{25{1'b0}}, Instruction[6:0]};  // Bit_Extender bit_extender_2
  Adder #(.width(32)) adder_1 (.a(Stack_Pointer), .b(bit_extender_1_out), .out(ADD));  // open: cin, cout
  Subtractor #(.width(32)) subtractor_1 (.a(Stack_Pointer), .b(bit_extender_2_out), .out(SUB));  // open: bin, bout
  Multiplexer #(.enable("false"), .width(32)) multiplexer_1 (
    .in0(ADD), .in1(SUB), .out(MUX_OUTPUT), .sel(Instruction[7]));
  Multiplexer #(.enable("false"), .width(32)) multiplexer_2 (
    .in0({32{1'b0}}), .in1(MUX_OUTPUT), .out(New_Stack_Pointer), .sel(Enable));

  assign Write_Enable = Enable;

  // Other names for the same wires on the sheet: IMM7[6:0] = Instruction[6:0]; INSTRUCT[15:0] = Instruction;
  //   ADD_OR_SUB_BIT = Instruction[7]; MUX_OUTPUT_AFTER_ENABLE_CHECK[31:0] = New_Stack_Pointer;
  //   SP[31:0] = Stack_Pointer

  // Notes on the sheet:
  //   Pull output low on Enable = 0
endmodule
