// Logisim project Ctl_Shift_Add_Sub_Mov.circ as structural Verilog: 4 circuits, main circuit Shift_Add_Sub_Mov
module Shift_Add_Sub_Mov (
  input  Enable,
  input  [15:0] Instruction,
  output [3:0] Flags_Update_Mask,
  output Carry,
  output Imm32_Enable,
  output [3:0] ALU_Opcode,
  output [2:0] Rm,
  output [2:0] Rd,
  output [2:0] Rn,
  output [4:0] Imm5,
  output [31:0] Imm32
);

  wire multiplexer_1_out, multiplexer_15_out;
  wire [2:0] ADD_IMM3_CONVERT, multiplexer_2_out, multiplexer_3_out, multiplexer_14_out, SUB_IMM3_CONVERT;
  wire [3:0] flag_update_circ_1_flag_mask_out, opcode_1_sortie, OPERATION_N;
  wire [4:0] ASR_IMM5, LSL_IMM5, LSR_IMM5, multiplexer_10_out;
  wire [7:0] ADD_IMM8_CONVERT, CMP_IMM8, MOV_IMM8, SUB_IMM8_CONVERT;
  wire [15:0] ADD_IMM3_OUT, ADD_REG_OUT, ASR_OUT, LSL_OUT, LSR_OUT, SUB_IMM3_OUT, SUB_REG_OUT;
  wire [15:8] ADD_IMM8_OUT, CMP_OUT, MOV_OUT, SUB_IMM8_OUT;
  wire [31:0] IMM32_OUT, multiplexer_8_out, negator_1_out;

  Demultiplexer #(.select(4), .width(16)) demultiplexer_1 (
    .out0({LSL_OUT[15:11], LSL_IMM5, LSL_OUT[5:0]}), .out1({LSR_OUT[15:11], LSR_IMM5, LSR_OUT[5:0]}),
    .out2({ASR_OUT[15:11], ASR_IMM5, ASR_OUT[5:0]}), .out3(ADD_REG_OUT), .out4(SUB_REG_OUT),
    .out5({ADD_IMM3_OUT[15:9], ADD_IMM3_CONVERT, ADD_IMM3_OUT[5:0]}),
    .out6({SUB_IMM3_OUT[15:9], SUB_IMM3_CONVERT, SUB_IMM3_OUT[5:0]}), .out7({MOV_OUT, MOV_IMM8}),
    .out8({CMP_OUT, CMP_IMM8}), .out9({ADD_IMM8_OUT, ADD_IMM8_CONVERT}),
    .out10({SUB_IMM8_OUT, SUB_IMM8_CONVERT}), .in(Instruction), .sel(OPERATION_N));  // open: out11, out12, out13, out14, out15
  // Probe on LSL_IMM5
  OPCODE_SIMPLIFIER opcode_simplifier_1 (.OPCODE_7BITS(Instruction[15:9]), .OPCODE_4BITS(OPERATION_N));
  // Probe on LSR_IMM5
  FLAG_UPDATE_CIRC flag_update_circ_1 (.OPCODE_IN(Instruction[15:9]), .FLAG_MASK_OUT(flag_update_circ_1_flag_mask_out));
  Multiplexer #(.select(4)) multiplexer_1 (
    .in0(1'b0), .in1(1'b0), .in2(1'b0), .in3(1'b0), .in4(1'b0), .in5(1'b1), .in6(1'b1), .in7(1'b1),
    .in8(1'b1), .in9(1'b1), .in10(1'b1), .out(multiplexer_1_out), .sel(OPERATION_N));  // open: in11, in12, in13, in14, in15
  Multiplexer #(.select(4), .width(3)) multiplexer_2 (
    .in0(LSL_OUT[5:3]), .in1(LSR_OUT[5:3]), .in2(ASR_OUT[5:3]), .in3(ADD_REG_OUT[8:6]),
    .in4(SUB_REG_OUT[8:6]), .in5(3'b000), .in6(3'b000), .in7(3'b000), .in8(3'b000), .in9(3'b000),
    .in10(3'b000), .in11(3'b000), .in12(3'b000), .in13(3'b000), .in14(3'b000), .in15(3'b000),
    .out(multiplexer_2_out), .sel(OPERATION_N));
  Multiplexer #(.select(4), .width(3)) multiplexer_3 (
    .in0(Rm), .in1(Rm), .in2(Rm), .in3(ADD_REG_OUT[5:3]), .in4(SUB_REG_OUT[5:3]), .in5(ADD_IMM3_OUT[5:3]),
    .in6(SUB_IMM3_OUT[5:3]), .in7(3'b000), .in8(3'b000), .in9(Rd), .in10(Rd), .in11(3'b000), .in12(3'b000),
    .in13(3'b000), .in14(3'b000), .in15(3'b000), .out(multiplexer_3_out), .sel(OPERATION_N));
  // Probe on OPERATION_N
  // Probe on ASR_IMM5
  Multiplexer #(.width(4)) multiplexer_4 (
    .in0(4'b0000), .in1(flag_update_circ_1_flag_mask_out), .out(Flags_Update_Mask), .sel(Enable));
  Multiplexer multiplexer_5 (.in0(1'b0), .in1(multiplexer_1_out), .out(Imm32_Enable), .sel(Enable));
  Multiplexer #(.width(3)) multiplexer_6 (.in0(3'b000), .in1(multiplexer_2_out), .out(Rm), .sel(Enable));
  Multiplexer #(.width(3)) multiplexer_7 (.in0(3'b000), .in1(multiplexer_3_out), .out(Rn), .sel(Enable));
  Negator #(.width(32)) negator_1 (.in(IMM32_OUT), .out(negator_1_out));
  Multiplexer #(.select(4), .width(32)) multiplexer_8 (
    .in0(IMM32_OUT), .in1(IMM32_OUT), .in2(IMM32_OUT), .in3(IMM32_OUT), .in4(IMM32_OUT), .in5(IMM32_OUT),
    .in6(IMM32_OUT), .in7(negator_1_out), .in8(IMM32_OUT), .in9(IMM32_OUT), .in10(IMM32_OUT),
    .in11(IMM32_OUT), .in12(IMM32_OUT), .in13(IMM32_OUT), .in14(IMM32_OUT), .in15(IMM32_OUT),
    .out(multiplexer_8_out), .sel(OPERATION_N));
  Multiplexer #(.width(5)) multiplexer_9 (.in0({5{1'b0}}), .in1(multiplexer_10_out), .out(Imm5), .sel(Enable));
  Multiplexer #(.select(4), .width(5)) multiplexer_10 (
    .in0(LSL_IMM5), .in1(LSR_IMM5), .in2(ASR_IMM5), .in3({5{1'b0}}), .in4({5{1'b0}}), .in5({5{1'b0}}),
    .in6({5{1'b0}}), .in7({5{1'b0}}), .in8({5{1'b0}}), .in9({5{1'b0}}), .in10({5{1'b0}}), .in11({5{1'b0}}),
    .in12({5{1'b0}}), .in13({5{1'b0}}), .in14({5{1'b0}}), .in15({5{1'b0}}), .out(multiplexer_10_out),
    .sel(OPERATION_N));
  Multiplexer #(.width(32)) multiplexer_11 (.in0({32{1'b0}}), .in1(multiplexer_8_out), .out(Imm32), .sel(Imm32_Enable));
  Multiplexer #(.select(4), .width(32)) multiplexer_12 (
    .in5({{29{1'b0}}, ADD_IMM3_CONVERT}), .in6({{29{1'b0}}, SUB_IMM3_CONVERT}), .in7({{24{1'b0}}, MOV_IMM8}),
    .in8({{24{1'b0}}, CMP_IMM8}), .in9({{24{1'b0}}, ADD_IMM8_CONVERT}),
    .in10({{24{1'b0}}, SUB_IMM8_CONVERT}), .out(IMM32_OUT), .sel(OPERATION_N));  // open: in0, in1, in2, in3, in4, in11, in12, in13, in14, in15
  Multiplexer #(.width(3)) multiplexer_13 (.in0(3'b000), .in1(multiplexer_14_out), .out(Rd), .sel(Enable));
  Multiplexer #(.select(4), .width(3)) multiplexer_14 (
    .in0(LSL_OUT[2:0]), .in1(LSR_OUT[2:0]), .in2(ASR_OUT[2:0]), .in3(ADD_REG_OUT[2:0]),
    .in4(SUB_REG_OUT[2:0]), .in5(ADD_IMM3_OUT[2:0]), .in6(SUB_IMM3_OUT[2:0]), .in7(MOV_OUT[10:8]),
    .in8(CMP_OUT[10:8]), .in9(ADD_IMM8_OUT[10:8]), .in10(SUB_IMM8_OUT[10:8]), .out(multiplexer_14_out),
    .sel(OPERATION_N));  // open: in11, in12, in13, in14, in15
  // Probe on IMM32_OUT
  Multiplexer #(.select(4)) multiplexer_15 (
    .in0(1'b0), .in1(1'b0), .in2(1'b0), .in3(1'b0), .in4(1'b1), .in5(1'b0), .in6(1'b1), .in7(1'b0),
    .in8(1'b0), .in9(1'b0), .in10(1'b1), .out(multiplexer_15_out), .sel(OPERATION_N));  // open: in11, in12, in13, in14, in15
  opcode opcode_1 (.Entree(Instruction[13:9]), .Sortie(opcode_1_sortie));
  Multiplexer multiplexer_16 (.in0(1'b0), .in1(multiplexer_15_out), .out(Carry), .sel(Enable));
  Multiplexer #(.width(4)) multiplexer_17 (.in0(4'b0000), .in1(opcode_1_sortie), .out(ALU_Opcode), .sel(Enable));

  // Other names for the same wires on the sheet: ADD_IMM3_IMM3[2:0] = ADD_IMM3_CONVERT;
  //   ADD_IMM3_OUT[8:6] = ADD_IMM3_CONVERT; ADD_IMM3_RD[2:0] = ADD_IMM3_OUT[2:0];
  //   ADD_IMM3_RN[2:0] = ADD_IMM3_OUT[5:3]; ADD_IMM8_IMM8[7:0] = ADD_IMM8_CONVERT;
  //   ADD_IMM8_OUT[7:0] = ADD_IMM8_CONVERT; ADD_IMM8_RD[2:0] = ADD_IMM8_OUT[10:8]; ADD_REG_RD[2:0] = ADD_REG_OUT[2:0];
  //   ADD_REG_RN[2:0] = ADD_REG_OUT[5:3]; ADD_REG_RM[2:0] = ADD_REG_OUT[8:6]; ASR_RD[2:0] = ASR_OUT[2:0];
  //   ASR_RM[2:0] = ASR_OUT[5:3]; ASR_OUT[10:6] = ASR_IMM5; CMP_IMM8_CONVERT[7:0] = CMP_IMM8; CMP_OUT[7:0] = CMP_IMM8;
  //   CMP_RD[2:0] = CMP_OUT[10:8]; DATA[15:0] = Instruction; alu_opcode_t[4:0] = Instruction[13:9];
  //   OPCODE_IN[6:0] = Instruction[15:9]; LSL_RD[2:0] = LSL_OUT[2:0]; LSL_RM[2:0] = LSL_OUT[5:3];
  //   LSL_OUT[10:6] = LSL_IMM5; LSR_RD[2:0] = LSR_OUT[2:0]; LSR_RM[2:0] = LSR_OUT[5:3]; LSR_OUT[10:6] = LSR_IMM5;
  //   MOV_IMM8_CONVERT[7:0] = MOV_IMM8; MOV_OUT[7:0] = MOV_IMM8; MOV_RD[2:0] = MOV_OUT[10:8];
  //   SUB_IMM3_IMM3[2:0] = SUB_IMM3_CONVERT; SUB_IMM3_OUT[8:6] = SUB_IMM3_CONVERT;
  //   SUB_IMM3_RD[2:0] = SUB_IMM3_OUT[2:0]; SUB_IMM3_RN[2:0] = SUB_IMM3_OUT[5:3];
  //   SUB_IMM8_IMM8[7:0] = SUB_IMM8_CONVERT; SUB_IMM8_OUT[7:0] = SUB_IMM8_CONVERT;
  //   SUB_IMM8_RD[2:0] = SUB_IMM8_OUT[10:8]; SUB_REG_RD[2:0] = SUB_REG_OUT[2:0]; SUB_REG_RN[2:0] = SUB_REG_OUT[5:3];
  //   SUB_REG_RM[2:0] = SUB_REG_OUT[8:6]

  // Notes on the sheet:
  //   Pull output low on Enable = 0
  //   Operation SELECTOR
  //   LSL assign
  //   SUB_REG assign
  //   CMP assign
  //   Note: ALU uses Rn register for shifts. Use Rn instead of Rm for shifts (immediate) here too
  //   Note 2: MOV uses RSB ALU opcode with Imm8 reversed so that it is copied to output register
  //   Note 3: Imm32_Enable forces the use of the immediate for Rm register
  //   LSR assign
  //   ADD_IMM3 assign
  //   ADD_IMM8 assign
  //   ASR assign
  //   SUB_IMM3 assign
  //   SUB_IMM8 assign
  //   ADD_REG assign
  //   MOV assign
  //   ALU will use Imm32 instead of Rm
  //   only ADD and SUB use Rm
  //   IMMX to IMM32
  //   Enable carry for SUB since it is reversed in ALU
endmodule

module OPCODE_SIMPLIFIER (
  input  [6:0] OPCODE_7BITS,
  output [3:0] OPCODE_4BITS
);

  wire not_1_out, not_2_out, not_3_out, not_4_out, not_5_out, or_1_out, or_2_out, or_3_out, or_4_out,
       or_5_out, or_6_out, or_7_out, or_8_out, or_9_out, or_10_out, or_11_out, or_12_out, or_13_out,
       or_14_out, or_15_out, or_16_out, or_17_out;

  not not_1 (not_1_out, OPCODE_7BITS[4]);
  not not_2 (not_2_out, OPCODE_7BITS[3]);
  not not_3 (not_3_out, OPCODE_7BITS[2]);
  not not_4 (not_4_out, OPCODE_7BITS[1]);
  not not_5 (not_5_out, OPCODE_7BITS[0]);
  or or_1 (or_1_out, OPCODE_7BITS[6], OPCODE_7BITS[5], OPCODE_7BITS[4]);
  or or_2 (or_2_out, OPCODE_7BITS[6], OPCODE_7BITS[5], OPCODE_7BITS[3], OPCODE_7BITS[2]);
  or or_3 (or_3_out, OPCODE_7BITS[6], OPCODE_7BITS[5], OPCODE_7BITS[4], OPCODE_7BITS[3]);
  or or_4 (or_4_out, OPCODE_7BITS[6], OPCODE_7BITS[5], OPCODE_7BITS[4], OPCODE_7BITS[2]);
  or or_5 (or_5_out, OPCODE_7BITS[6], OPCODE_7BITS[5], OPCODE_7BITS[4], OPCODE_7BITS[1], OPCODE_7BITS[0]);
  or or_6 (or_6_out, OPCODE_7BITS[6], OPCODE_7BITS[5], OPCODE_7BITS[3], not_3_out);
  or or_7 (or_7_out, OPCODE_7BITS[6], OPCODE_7BITS[5], not_2_out, OPCODE_7BITS[2]);
  or or_8 (or_8_out, OPCODE_7BITS[6], OPCODE_7BITS[5], not_3_out, OPCODE_7BITS[1], OPCODE_7BITS[0]);
  or or_9 (or_9_out, OPCODE_7BITS[6], OPCODE_7BITS[5], not_1_out, not_3_out);
  or or_10 (or_10_out, OPCODE_7BITS[6], OPCODE_7BITS[5], OPCODE_7BITS[4], OPCODE_7BITS[3]);
  or or_11 (or_11_out, OPCODE_7BITS[6], OPCODE_7BITS[5], OPCODE_7BITS[4], not_3_out, OPCODE_7BITS[1], not_5_out);
  or or_12 (or_12_out, OPCODE_7BITS[6], OPCODE_7BITS[5], OPCODE_7BITS[4], not_3_out, not_4_out, OPCODE_7BITS[0]);
  or or_13 (or_13_out, OPCODE_7BITS[6], OPCODE_7BITS[5], OPCODE_7BITS[3], not_3_out);
  or or_14 (or_14_out, OPCODE_7BITS[6], OPCODE_7BITS[5], not_1_out, not_2_out, OPCODE_7BITS[2]);
  or or_15 (or_15_out, OPCODE_7BITS[6], OPCODE_7BITS[5], OPCODE_7BITS[4], OPCODE_7BITS[2]);
  or or_16 (or_16_out, OPCODE_7BITS[6], OPCODE_7BITS[5], not_1_out, not_3_out);
  or or_17 (or_17_out, OPCODE_7BITS[6], OPCODE_7BITS[5], OPCODE_7BITS[4], not_2_out, not_5_out);
  and and_1 (OPCODE_4BITS[3], or_1_out, or_2_out);
  and and_2 (OPCODE_4BITS[2], or_3_out, or_4_out, or_5_out, or_6_out, or_7_out, or_8_out, or_9_out);
  and and_3 (OPCODE_4BITS[1], or_10_out, or_11_out, or_12_out, or_13_out, or_14_out);
  and and_4 (OPCODE_4BITS[0], or_15_out, or_16_out, or_17_out);
endmodule

module FLAG_UPDATE_CIRC (
  input  [6:0] OPCODE_IN,
  output [3:0] FLAG_MASK_OUT
);

  wire [3:0] OPERATION;

  OPCODE_SIMPLIFIER opcode_simplifier_1 (.OPCODE_7BITS(OPCODE_IN), .OPCODE_4BITS(OPERATION));
  Multiplexer #(.select(4), .width(4)) multiplexer_1 (
    .in0(4'b1110), .in1(4'b1110), .in2(4'b1110), .in3(4'b1111), .in4(4'b1111), .in5(4'b1111), .in6(4'b1111),
    .in7(4'b1100), .in8(4'b1111), .in9(4'b1111), .in10(4'b1111), .out(FLAG_MASK_OUT), .sel(OPERATION));  // open: in11, in12, in13, in14, in15
endmodule

module opcode (
  input  [4:0] Entree,
  output [3:0] Sortie
);

  wire and_2_out, and_3_out, and_4_out, and_5_out, and_6_out, and_7_out, not_1_out, not_2_out, not_3_out,
       not_4_out;

  not not_1 (not_1_out, Entree[4]);
  not not_2 (not_2_out, Entree[3]);
  not not_3 (not_3_out, Entree[2]);
  not not_4 (not_4_out, Entree[0]);
  and and_1 (Sortie[3], Entree[4], not_2_out);
  and and_2 (and_2_out, not_1_out, not_2_out);
  and and_3 (and_3_out, Entree[2], Entree[0]);
  and and_4 (and_4_out, Entree[4], Entree[2]);
  and and_5 (and_5_out, not_1_out, not_2_out, Entree[2]);
  and and_6 (and_6_out, not_1_out, Entree[2], not_4_out);
  and and_7 (and_7_out, Entree[4], not_3_out);
  or or_1 (Sortie[1], and_2_out, and_3_out, and_4_out);
  or or_2 (Sortie[0], and_5_out, and_6_out, and_7_out);

  assign Sortie[2] = Entree[3];
endmodule
