// Logisim project SR_Ctl_Logical_Shift_Right.circ as structural Verilog: 1 circuit, main circuit main
module main (
  input  in_1
);

  wire [15:0] data;

  Register #(.width(16)) register_1 (.D(data));  // open: en, clk, Q, clr
endmodule
