// Logisim project SR_LSR.circ as structural Verilog: 1 circuit, main circuit main
module main (
  input  [15:0] Data_IN
);

  wire [2:0] RD;

  Shifter #(.shift("lr"), .width(3)) shifter_1 (.in(Data_IN[5:3]), .\dist (Data_IN[7:6]), .out(RD));
  Decoder decoder_1 ();  // open: out0, out1, sel, en
  // Pins of 2 and 5 bits meet at Data_IN[10:6]
endmodule
