// Logisim project SR_OPSELECTOR.circ as structural Verilog: 2 circuits, main circuit main
module main (
  input  [4:0] op_code
);
endmodule

module OPSELECTOR (
  input  [3:0] op_code,
  input  [15:0] data,
  output [3:0] SR_OUT
);

  wire and_2_out, and_3_out, and_4_out, and_5_out, and_6_out, not_1_out, not_2_out, not_3_out, not_4_out;

  not not_1 (not_1_out, op_code[3]);
  not not_2 (not_2_out, op_code[2]);
  not not_3 (not_3_out, op_code[1]);
  not not_4 (not_4_out, op_code[0]);
  and and_1 (SR_OUT[3], not_1_out, op_code[2], op_code[1], op_code[0]);
  and and_2 (and_2_out, not_1_out, not_2_out, op_code[1], op_code[0]);
  and and_3 (and_3_out, not_1_out, op_code[2], not_3_out);
  and and_4 (and_4_out, not_1_out, op_code[2], not_4_out);
  and and_5 (and_5_out, not_1_out, not_3_out, op_code[0]);
  and and_6 (and_6_out, not_1_out, op_code[1], not_4_out);
  and and_7 (SR_OUT[0], not_1_out, not_4_out);
  or or_1 (SR_OUT[2], and_2_out, and_3_out, and_4_out);
  or or_2 (SR_OUT[1], and_5_out, and_6_out);
  Decoder #(.select(4)) decoder_1 (.sel(SR_OUT));  // open: out0, out1, out2, out3, out4, out5, out6, out7, out8, out9, out10, out11, out12, out13, out14, out15, en
endmodule
